# Fritzing sketch nixie_i2c_driver_stackable_v2 (saved by Fritzing 0.9.3b)
circuit board: 5.09512cm x 6.0163cm

parts:
  I2C_-_PCF8574 = PCF8574 [package="DIP16 [THT]"]
  STACK_PWR = SIP - 2 pins [chip_label=PWR package="SIP (Single Inline) [THT]"]
  I2C = SIP - 2 pins [chip_label=Bus package="SIP (Single Inline) [THT]"]
  SW1 = DIP SWITCH [package=dipswitch-02]
  SW2 = DIP SWITCH [package=dipswitch-02]
  R2 = Resistor [tolerance=±5% resistance=10k package=THT]
  C1 = Tantalum Capacitor [capacitance=0.1µF package="100 mil [THT, tantalum]"]
  C2 = Tantalum Capacitor [capacitance=0.1µF package="100 mil [THT, tantalum]"]
  C3 = Tantalum Capacitor [capacitance=0.1µF package="100 mil [THT, tantalum]"]
  R1 = Resistor [tolerance=±5% resistance=10k package=THT]
  R3 = Resistor [tolerance=±5% resistance=10k package=THT]
  R4 = Resistor [tolerance=±5% resistance=10k package=THT]
  R5 = Resistor [tolerance=±5% resistance=10k package=THT]
  Anode = double row male pin header, 6 pins [form="♂ (male)"]
  R6 = Resistor [tolerance=±5% resistance=10 power=2W package=THT]
  R7 = Resistor [tolerance=±5% resistance=10 power=2W package=THT]
  R8 = Resistor [tolerance=±5% resistance=10k package=THT]
  74141 = IC, DIP package, 16 pins [chip_label=74141]
  NX_1 = double row male pin header, 10 pins [form="♂ (male)"]
  NX_2 = double row male pin header, 10 pins [form="♂ (male)"]
  74141_2 = IC, DIP package, 16 pins [chip_label=74141]
  HV_PWR = IC, SIP package, 6 pins [chip_label=IC]

nets:
  N1: I2C_-_PCF8574.A0, SW1.1, R5.Pin_0
  N2: I2C_-_PCF8574.A1, SW2.2, R4.Pin_0
  N3: I2C_-_PCF8574.A3, SW2.1, R3.Pin_0
  A0: I2C_-_PCF8574.P0, 74141_2.pin3
  B0: I2C_-_PCF8574.P1, 74141_2.pin6
  C0: I2C_-_PCF8574.P2, 74141_2.pin7
  D0: I2C_-_PCF8574.P3, 74141_2.pin4
  D1/GND: I2C_-_PCF8574.GND, I2C_-_PCF8574.P7, STACK_PWR.pin2, C1.-, C2.-, C3.-, R3.Pin_1, R4.Pin_1, R5.Pin_1, R8.Pin_1, 74141.pin4, 74141.pin12, 74141_2.pin12, HV_PWR.pin2, HV_PWR.pin4
  A1: I2C_-_PCF8574.P4, 74141.pin3
  B1: I2C_-_PCF8574.P5, 74141.pin6
  C1: I2C_-_PCF8574.P6, 74141.pin7
  N4: I2C_-_PCF8574.SCL, I2C.pin2, R2.Pin_1
  N5: I2C_-_PCF8574.SDA, I2C.pin1, R1.Pin_1
  5V: I2C_-_PCF8574.VCC, STACK_PWR.pin1, SW1.3, SW1.4, SW2.3, SW2.4, R2.Pin_0, C1.+, C2.+, C3.+, R1.Pin_0, 74141.pin5, 74141_2.pin5
  HV EN: SW1.2, R8.Pin_0, HV_PWR.pin3
  N6: Anode.pin1, Anode.pin2, Anode.pin3, R6.Pin_1
  N7: Anode.pin4, Anode.pin5, Anode.pin6, R7.Pin_1
  170V: R6.Pin_0, R7.Pin_0, HV_PWR.pin5, HV_PWR.pin6
  N8: 74141.pin1, NX_2.pin9
  N9: 74141.pin2, NX_2.pin10
  N10: 74141.pin8, NX_2.pin3
  N11: 74141.pin9, NX_2.pin4
  N12: 74141.pin10, NX_2.pin8
  N13: 74141.pin11, NX_2.pin7
  N14: 74141.pin13, NX_2.pin5
  N15: 74141.pin14, NX_2.pin6
  N16: 74141.pin15, NX_2.pin2
  N17: 74141.pin16, NX_2.pin1
  N18: NX_1.pin1, 74141_2.pin16
  N19: NX_1.pin2, 74141_2.pin15
  N20: NX_1.pin3, 74141_2.pin8
  N21: NX_1.pin4, 74141_2.pin9
  N22: NX_1.pin5, 74141_2.pin13
  N23: NX_1.pin6, 74141_2.pin14
  N24: NX_1.pin7, 74141_2.pin11
  N25: NX_1.pin8, 74141_2.pin10
  N26: NX_1.pin9, 74141_2.pin1
  N27: NX_1.pin10, 74141_2.pin2

notes:
  Nixie i2c Driver, This chip is indended to be used with angled pin headers for the nixie tubes in order to stack the modules on top of each other, 1
  vin gnd en gnd hv hv
  5v gnd
  SCL SDA
  A2 A1 A0 EN
  4 3 2 1 0
  5 6 7 8 9
  Nixie i2c Driver
  rev 2 - 10.12.2017
  Supply HV power here. Matching small HV modules can be stacked on top.
  When stacking, the topmost driver can supply power to all modules below
  The i2c driver is dynamically adressable using the three dip switches
  The fourth switch is used to enable / disable the HV module. Note: some hv modules have an inverten EN input!
  Pin 1 -> 0
  Pin 10 -> 9
  IN-4 tubes have 3 anodes but the driver supports all kinds of nixie tubes
